// Logisim project 2313.circ as structural Verilog: 12 circuits, main circuit main
module main (
  input  A,
  input  in_2,
  input  in_3,
  input  B,
  input  in_5,
  input  in_6,
  output out_7,
  output out_8,
  output out_9,
  output out_10
);

  wire full_adder_2_carrt_out, full_adder_3_carrt_out;

  Full_Adder full_adder_1 (.A(full_adder_2_carrt_out), .B(A), .C(B), .SUM(out_8), .Carrt_out(out_7));
  Full_Adder full_adder_2 (
    .A(full_adder_3_carrt_out), .B(in_2), .C(in_5), .SUM(out_9), .Carrt_out(full_adder_2_carrt_out));
  Full_Adder full_adder_3 (.A(1'b0), .B(in_3), .C(in_6), .SUM(out_10), .Carrt_out(full_adder_3_carrt_out));
endmodule

module Full_Adder (
  input  A,
  input  B,
  input  C,
  output SUM,
  output Carrt_out
);

  wire and_1_out, and_2_out, xor_1_out;

  xor xor_1 (xor_1_out, A, B);
  and and_1 (and_1_out, xor_1_out, C);
  and and_2 (and_2_out, A, B);
  xor xor_2 (SUM, xor_1_out, C);
  or or_1 (Carrt_out, and_1_out, and_2_out);
endmodule

module _2_bit_adder (
  input  A,
  input  in_2,
  input  B,
  input  in_4,
  output out_5,
  output out_6,
  output out_7
);

  wire full_adder_2_carrt_out;

  Full_Adder full_adder_1 (.A(full_adder_2_carrt_out), .B(B), .C(A), .SUM(out_7), .Carrt_out(out_6));
  Full_Adder full_adder_2 (.A(1'b0), .B(in_4), .C(in_2), .SUM(out_5), .Carrt_out(full_adder_2_carrt_out));
endmodule

module decoder (
  input  A,
  input  B,
  output line0,
  output line1,
  output line2,
  output line3
);

  wire not_1_out, not_2_out, not_3_out, not_4_out;

  not not_1 (not_1_out, B);
  not not_2 (not_2_out, A);
  not not_3 (not_3_out, A);
  not not_4 (not_4_out, B);
  and and_1 (line0, not_1_out, not_2_out);
  and and_2 (line1, not_3_out, B);
  and and_3 (line2, not_4_out, A);
  and and_4 (line3, A, B);

  // Notes on the sheet:
  //   decode binary to line number
endmodule

module encoder (
  input  line0,
  input  line_2,
  input  line3,
  input  line_3,
  output A,
  output B
);

  or or_1 (A, line3, line_3);
  or or_2 (B, line_2, line_3);

  // Notes on the sheet:
  //   encode line number to binary
endmodule

module priority_encoder (
  input  L0,
  input  L1,
  input  L2,
  input  L3,
  output validation,
  output A,
  output B
);

  wire and_1_out, not_1_out;

  not not_1 (not_1_out, L2);
  and and_1 (and_1_out, L1, not_1_out);
  or or_1 (B, and_1_out, L3);
  or or_2 (A, L2, L3);
  or or_3 (validation, L0, L1, L2, L3);

  // Notes on the sheet:
  //   do the highest first, if L1 and L3 are selected, only encode L3
  //   when line/lines is/are selected, it is 1
endmodule

module mutiplexers (
  input  control,
  input  Control1,
  input  control2,
  input  A,
  input  control_2,
  input  A_2,
  input  A_3,
  input  B,
  input  B_2,
  input  C,
  input  D,
  output \output ,
  output output_2,
  output output_3
);

  wire _00_out, _01_out, _10_out, _11_out, and_1_out, and_2_out, not_1_out, not_2_out, not_3_out, not_4_out,
       not_5_out;

  not not_1 (not_1_out, control_2);
  xor xor_1 (\output , control, A);
  and and_1 (and_1_out, not_1_out, A_3);
  and and_2 (and_2_out, B_2, control_2);
  or or_1 (output_3, and_1_out, and_2_out);
  not not_2 (not_2_out, control2);
  and _00 (_00_out, not_2_out, not_3_out, A_2);
  not not_3 (not_3_out, Control1);
  not not_4 (not_4_out, control2);
  and _01 (_01_out, not_4_out, not_5_out, B);
  not not_5 (not_5_out, Control1);
  and _10 (_10_out, control2, Control1, C);
  and _11 (_11_out, control2, Control1, D);
  or or_2 (output_2, _00_out, _01_out, _10_out, _11_out);

  // Notes on the sheet:
  //   when control is 0, ouput A. when control is 1, output B
  //   put not gate if 0 is on the front
endmodule

module Demultiplexers (
  input  control1,
  input  control2,
  input  \input ,
  output line0,
  output line1,
  output line2,
  output line3
);

  wire not_1_out, not_2_out, not_3_out, not_4_out;

  not not_1 (not_1_out, control2);
  not not_2 (not_2_out, control1);
  not not_3 (not_3_out, control1);
  not not_4 (not_4_out, control2);
  and and_1 (line0, not_1_out, \input , not_2_out);
  and and_2 (line1, not_3_out, \input , control2);
  and and_3 (line2, not_4_out, \input , control1);
  and and_4 (line3, control1, \input , control2);

  // Notes on the sheet:
  //   decoder, add one input
endmodule

module inverter (
  input  in_1,
  input  in_2,
  input  in_3,
  input  Control_gate,
  input  in_5,
  input  in_6,
  input  in_7,
  input  in_8,
  input  in_9,
  input  in_10,
  input  control,
  output out_12,
  output out_13,
  output out_14,
  output overflow,
  output out_16,
  output out_17,
  output out_18,
  output overflow_2,
  output out_20,
  output out_21,
  output out_22
);

  wire HA_2_carry, HA_3_carry, HA_5_carry, HA_6_carry, not_1_out, not_2_out, not_3_out, xor_2_out, xor_4_out,
       xor_6_out;

  xor xor_1 (out_12, in_1, Control_gate);
  xor xor_2 (xor_2_out, in_8, control);
  Half_Adder HA (.A(HA_2_carry), .B(xor_2_out), .sum(out_20), .carry(overflow_2));
  xor xor_3 (out_13, in_2, Control_gate);
  xor xor_4 (xor_4_out, control, in_9);
  Half_Adder HA_2 (.A(HA_3_carry), .B(xor_4_out), .sum(out_21), .carry(HA_2_carry));
  xor xor_5 (out_14, in_3, Control_gate);
  xor xor_6 (xor_6_out, control, in_10);
  Half_Adder HA_3 (.A(control), .B(xor_6_out), .sum(out_22), .carry(HA_3_carry));
  not not_1 (not_1_out, in_5);
  not not_2 (not_2_out, in_6);
  Half_Adder HA_4 (.A(HA_6_carry), .B(not_1_out), .sum(out_16), .carry(overflow));
  not not_3 (not_3_out, in_7);
  Half_Adder HA_5 (.A(1'b1), .B(not_3_out), .sum(out_18), .carry(HA_5_carry));
  Half_Adder HA_6 (.A(HA_5_carry), .B(not_2_out), .sum(out_17), .carry(HA_6_carry));

  // Notes on the sheet:
  //   control one's complememnt inverter
  //   two's complement inverter with control
  //   two's complement inverter
endmodule

module Half_Adder (
  input  A,
  input  B,
  output sum,
  output carry
);

  xor xor_1 (sum, A, B);
  and and_1 (carry, B, A);
endmodule

module _1_bit_comparator (
  input  A,
  input  B,
  output smaller,
  output equal,
  output greater
);

  wire not_1_out, not_3_out, xor_1_out;

  not not_1 (not_1_out, A);
  and and_1 (smaller, not_1_out, B);
  xor xor_1 (xor_1_out, A, B);
  not not_2 (equal, xor_1_out);
  not not_3 (not_3_out, B);
  and and_2 (greater, A, not_3_out);
endmodule

module _2_bits_comparator (
  input  in_1,
  input  in_2,
  input  in_3,
  input  in_4,
  output equal,
  output greater
);

  wire and_2_out, and_3_out, not_1_out, not_2_out, not_4_out, xor_1_out, xor_2_out;

  xor xor_1 (xor_1_out, in_1, in_3);
  not not_1 (not_1_out, xor_1_out);
  and and_1 (equal, not_1_out, not_2_out);
  xor xor_2 (xor_2_out, in_2, in_4);
  not not_2 (not_2_out, xor_2_out);
  // NOT_Gate not_3 has open pins: in=in_3, out=open
  and and_2 (and_2_out, not_1_out, and_3_out);
  or or_1 (greater, in_1, and_2_out);
  not not_4 (not_4_out, in_4);
  and and_3 (and_3_out, not_4_out, in_2);
endmodule
